# Fritzing sketch ESP32 - DHT (saved by Fritzing 0.9.3b)
breadboards: 2

parts:
  U1 = NodeMCU V1.0
  R1 = Rotary Potentiometer (Small) [maximum_resistance=100kΩ package=THT]
  LED1 = smd LED [color="Red (633nm)" package="0603 [SMD]"]
  part = Resistor [tolerance=±5% resistance=330 package=THT]
  DHT22 = Humidity and Temperature Sensor RHT03 [part_number=TEMP/HUM]
  part_2 = Resistor [tolerance=±5% resistance=10k package=THT]

nets:
  N1: U1.D0, DHT22.Data-signal, part_2.Pin_1
  3V3: U1.3V3, R1.leg1, DHT22.Vcc, part_2.Pin_0
  N2: U1.GND, R1.leg2, part.Pin_0, DHT22.GND_2
  N3: U1.RX, LED1.anode
  N4: U1.RSV#41, R1.wiper
  N5: LED1.cathode, part.Pin_1

notes:
  ESP32
  GPIO 36
  (ADC 0)
  GPIO 2
  (LED)
  GPIO 23
  (DHT22)

custom parts:
  NodeMCU V1.0: ESP8266 based NodeMCU
