# Fritzing sketch ESP32 - DHT - OLED (saved by Fritzing 0.9.3b)
breadboards: 2

parts:
  U1 = NodeMCU V1.0
  R1 = Rotary Potentiometer (Small) [maximum_resistance=100kΩ package=THT]
  LED1 = smd LED [color="Red (633nm)" package="0603 [SMD]"]
  R2 = Resistor [tolerance=±5% resistance=330 package=THT]
  DHT22 = Humidity and Temperature Sensor RHT03 [part_number=TEMP/HUM]
  R3 = Resistor [tolerance=±5% resistance=10k package=THT]
  OLED_128_x_32 = Grove OLED 128x96

nets:
  N1: U1.D0, DHT22.Data-signal, R3.Pin_1
  N2: U1.D1, OLED_128_x_32.SCL
  N3: U1.D4, OLED_128_x_32.SDA
  VCC: U1.3V3, R1.leg1, DHT22.Vcc, R3.Pin_0, OLED_128_x_32.VCC
  GND: U1.GND, R1.leg2, R2.Pin_0, DHT22.GND_2, OLED_128_x_32.GND
  N4: U1.RX, LED1.anode
  N5: U1.RSV#41, R1.wiper
  N6: LED1.cathode, R2.Pin_1

notes:
  ESP32
  GPIO 36
  (ADC 0)
  GPIO 2
  (LED)
  GPIO 23
  (DHT22)
  SDA GPIO 21
  SCL GPIO 22

custom parts:
  NodeMCU V1.0: ESP8266 based NodeMCU
